// Logisim project additionneurComplet-tp1-060224.circ as structural Verilog: 1 circuit, main circuit main
module main (
  input  in_1,
  input  in_2,
  input  in_3,
  output out_4,
  output out_5
);

  wire AND_2_out, AND_out, XOR_out;

  xor XOR (XOR_out, in_2, in_3);
  and AND (AND_out, in_2, in_3);
  and AND_2 (AND_2_out, in_1, XOR_out);
  xor XOR_2 (out_4, in_1, XOR_out);
  or OR (out_5, AND_2_out, AND_out);

  // Notes on the sheet:
  //   ADDITIONNEUR COMPLET
endmodule
