// Logisim project demiAdditionneur-tP1-060224.circ as structural Verilog: 1 circuit, main circuit main
module main (
  input  in_1,
  input  in_2,
  output out_3,
  output [1:0] out_4,
  output out_5
);

  xor XOR__Ou_exclusif (out_3, in_1, in_2);
  and AND (out_4[1], in_1, in_2);

  assign out_4[0] = out_3;
  assign out_5 = out_4[1];

  // Notes on the sheet:
  //   TABLE DE VERITE XOR
  //   a    b    a ou !b
  //   0    0     0
  //   0    1     1
  //   1    0     1
  //   1    1     0
  //   Demi-additionneur
  //   TABLE AND
  //   a    b     a . b
  //   0    0     0
  //   0    1     0
  //   1    0     0
  //   1    1     1
endmodule
