// Logisim project horlogeNumerique-tp1-060224.circ as structural Verilog: 1 circuit, main circuit main
module main (
);

  wire and_1_out, clock_1_out, counter_1_carry, counter_3_carry, counter_4_carry, counter_5_carry,
       counter_6_carry, not_1_out, not_2_out, not_3_out, not_4_out, not_5_out;
  wire [3:0] counter_1_q, counter_2_q, counter_3_q, counter_4_q, counter_5_q, counter_6_q;

  and and_1 (and_1_out, counter_2_q[1], counter_1_q[2]);
  Clock clock_1 (.out(clock_1_out));
  Hex_Digit_Display hex_digit_display_1 (.value(counter_2_q));  // open: dp
  Hex_Digit_Display hex_digit_display_2 (.value(counter_1_q));  // open: dp
  Counter #(.width(4), .max('h9)) counter_1 (
    .Q(counter_1_q), .carry(counter_1_carry), .clk(not_1_out), .clr(and_1_out));  // open: load, D, count
  Counter #(.width(4), .max('h2)) counter_2 (
    .Q(counter_2_q), .clk(not_2_out), .clr(and_1_out));  // open: load, D, count, carry
  not not_1 (not_1_out, counter_3_carry);
  not not_2 (not_2_out, counter_1_carry);
  Hex_Digit_Display hex_digit_display_3 (.value(counter_4_q));  // open: dp
  Hex_Digit_Display hex_digit_display_4 (.value(counter_3_q));  // open: dp
  Counter #(.width(4), .max('h5)) counter_3 (
    .Q(counter_3_q), .carry(counter_3_carry), .clk(not_4_out));  // open: load, D, count, clr
  Counter #(.width(4), .max('h9)) counter_4 (
    .Q(counter_4_q), .carry(counter_4_carry), .clk(not_3_out));  // open: load, D, count, clr
  not not_3 (not_3_out, counter_5_carry);
  not not_4 (not_4_out, counter_4_carry);
  Hex_Digit_Display hex_digit_display_5 (.value(counter_5_q));  // open: dp
  Counter #(.width(4), .max('h5)) counter_5 (
    .Q(counter_5_q), .carry(counter_5_carry), .clk(not_5_out));  // open: load, D, count, clr
  not not_5 (not_5_out, counter_6_carry);
  Hex_Digit_Display hex_digit_display_6 (.value(counter_6_q));  // open: dp
  Counter #(.width(4), .max('h9)) counter_6 (
    .Q(counter_6_q), .carry(counter_6_carry), .clk(clock_1_out));  // open: load, D, count, clr

  // Notes on the sheet:
  //   HORLOGE NUMERIQUE
endmodule
